# Fritzing sketch c3 (saved by Fritzing 0.9.3b)
breadboards: 1

parts:
  Raspberry_Pi_1 = Raspberry Pi 3 [part_number=RPI-3-V1.2]
  LED1 = LED - 5mm [color="Green (570nm)" package="5 mm [THT]"]
  S1 = Pushbutton [package="[THT]"]
  R4 = Resistor [tolerance=±5% resistance=220 package=THT]
  LED2 = LED - 5mm [color="Blue (525nm)" package="5 mm [THT]"]
  LED3 = LED - 5mm [color="Red (633nm)" package="5 mm [THT]"]
  R5 = Resistor [tolerance=±5% resistance=220 package=THT]
  R6 = Resistor [tolerance=±5% resistance=220 package=THT]
  R7 = Resistor [tolerance=±5% resistance=220 package=THT]

nets (from the breadboard view):
  3V3: Raspberry_Pi_1.3v3, Raspberry_Pi_1.3V3, S1.Pin_3, S1.Pin_4
  N1: Raspberry_Pi_1.GPIO17, LED3.cathode
  N2: Raspberry_Pi_1.GPIO27, LED1.cathode
  N3: Raspberry_Pi_1.GND, R4.Pin_0, R5.Pin_0, R6.Pin_0, R7.Pin_1
  N4: Raspberry_Pi_1.GPIO24, S1.Pin_1, S1.Pin_2, R7.Pin_0
  N5: Raspberry_Pi_1.GPIO18, LED2.cathode
  N6: LED1.anode, R4.Pin_1
  N7: LED2.anode, R5.Pin_1
  N8: LED3.anode, R6.Pin_1

notes:
  Circuito 3
